# Fritzing sketch MagSpoofV2R6 (saved by Fritzing 0.9.3b)
circuit board: 8.97001cm x 3.49999cm
breadboards: 1

parts:
  LED1 = smd LED [color="Red (633nm)" package="1206 [SMD]"]
  R1 = Resistor [tolerance=±5% resistance=220 package="0805 [SMD]"]
  IC2_L293DD = SO20W [chip_label=SO20W package=SO(w)]
  S1 = SPST Switch [package=ayz0202]
  IC1 = Voltage Regulator [package=sot223]
  ANT = female pin header, 1 pin [form="♀ (female)"]
  ANT_2 = female pin header, 1 pin [form="♀ (female)"]
  J5 = female pin header, 11 pins [form="♀ (female)"]
  C5 = Capacitor Polarized [package=eia6032]
  C4 = Capacitor Polarized [package=eia6032]
  Batt+ = Pad [width=5.314926728805613 height=3.5384351006193211 connect=center]
  Batt- = Pad [width=5.314926728805613 height=3.5384351006193211 connect=center]
  null1 = Pad [width=3.2999999999999998 height=1.8 connect=center]  # not connected
  RX1 = Pad [width=3.2999999999999998 height=1.8 connect=center]
  GND1 = Pad [width=3.2999999999999998 height=1.8 connect=center]
  VCC1 = Pad [width=3.2999999999999998 height=1.8 connect=center]
  foo4 = Pad [width=3.2999999999999998 height=1.8 connect=center]  # not connected
  TX1 = Pad [width=3.2999999999999998 height=1.8 connect=center]
  TX = Pad [width=3.2999999999999998 height=1.8 connect=center]
  RX = Pad [width=3.2999999999999998 height=1.8 connect=center]
  G = Pad [width=3.2999999999999998 height=1.8 connect=center]
  VC = Pad [width=3.2999999999999998 height=1.8 connect=center]
  RS = Pad [width=3.2999999999999998 height=1.8 connect=center]
  D7 = Pad [width=3.2999999999999998 height=1.8 connect=center]
  D8 = Pad [width=3.2999999999999998 height=1.8 connect=center]
  D9 = Pad [width=3.2999999999999998 height=1.8 connect=center]
  D10 = Pad [width=3.2999999999999998 height=1.8 connect=center]
  D16 = Pad [width=3.2999999999999998 height=1.8 connect=center]
  D14 = Pad [width=3.2999999999999998 height=1.8 connect=center]
  D15 = Pad [width=3.2999999999999998 height=1.8 connect=center]
  A0 = Pad [width=3.2999999999999998 height=1.8 connect=center]
  VS = Pad [width=3.2999999999999998 height=1.8 connect=center]  # not connected
  A1 = Pad [width=3.2999999999999998 height=1.8 connect=center]
  S2 = SWITCH-MOMENTARY-2 [package=tactile_switch_tall]
  D2 = Pad [width=3.2999999999999998 height=1.8 connect=center]

nets:
  N1: LED1.cathode, IC2_L293DD.4, IC2_L293DD.5, IC2_L293DD.6, IC2_L293DD.7, IC2_L293DD.11, IC2_L293DD.12, IC2_L293DD.13, IC2_L293DD.14, IC2_L293DD.15, IC2_L293DD.16, IC2_L293DD.17, IC2_L293DD.18, IC2_L293DD.19, IC1.ADJ, J5.pin1, C5.-, C4.-, Batt-.pad, GND1.pad, G.pad
  N2: LED1.anode, R1.Pin_1
  N3: R1.Pin_0, D2.pad
  N4: IC2_L293DD.1, A0.pad
  N5: IC2_L293DD.2, D10.pad
  N6: IC2_L293DD.3, ANT_2.pin1, J5.pin7
  N7: IC2_L293DD.8, ANT.pin1, J5.pin6
  N8: IC2_L293DD.9, D9.pad
  N9: IC2_L293DD.10, S1.S, IC1.IN, C4.+
  N10: IC2_L293DD.20, IC1.OUT, J5.pin3, C5.+, VCC1.pad, VC.pad
  N11: S1.P, Batt+.pad
  N12: J5.pin2, RS.pad
  N13: J5.pin4, RX1.pad, TX.pad
  N14: J5.pin5, TX1.pad, RX.pad
  N15: J5.pin8, D15.pad
  N16: J5.pin9, D14.pad
  N17: J5.pin10, D16.pad
  N18: J5.pin11, A1.pad
  N19: D7.pad, S2.2
  N20: D8.pad, S2.1

notes:
  G
  RS
  TX
  RX
  ANT
  SCK
  MISO
  MOSI
  A1
  VC
  .
